// Logisim project SmartParking (1).circ as structural Verilog: 1 circuit, main circuit main
module main (
  input  S1,
  input  S2,
  input  S3,
  input  S4,
  input  CAR
);

  wire and_1_out, and_2_out, not_1_out, not_4_out, not_5_out;
  wire [2:0] bitadder_1_out;
  wire [3:0] bitextender_1_p5, undriven;

  not not_1 (not_1_out, S1);
  not not_2 (undriven[1], S2);
  not not_3 (undriven[1], S3);
  not not_4 (not_4_out, S4);
  LED FULL (.in(and_1_out));
  and and_1 (and_1_out, S1, S2, S3, S4);
  not not_5 (not_5_out, and_1_out);
  BitAdder #(.width(1)) bitadder_1 (.in1(undriven[0]), .out(bitadder_1_out));  // open: in0, in2, in3
  and and_2 (and_2_out, not_5_out, CAR);
  LED GATE_OPEN (.in(and_2_out));
  // BitExtender #(.in_width(3), .out_width(4)) bitextender_1: pin names not known; wires that end beside it: not_1_out, undriven[1], not_4_out, bitadder_1_out, bitextender_1_p5
  Hex_Digit_Display hex_digit_display_1 (.value(bitextender_1_p5));  // open: dp
  // Pins of 1 and 4 bits meet at undriven
endmodule
